# Fritzing sketch Tea-Duino Schematic (saved by Fritzing 0.8.7b)
breadboards: 1

parts:
  DIP-Relay1 = DIP-Relay-D31A [part_number=D31A*]
  U1 = POT [package=alps_pot]
  Q2 = TRANSISTOR_NPN [package=to-92-ammo]
  Part1 = Arduino Uno (Rev3)
  LCD1 = LCD screen
  Part2 = Thumb Joystick
  D1 = Rectifier Diode [package="Melf DO-213 AA [SMD]"]
  S1 = Round Pushbutton

nets:
  N1: DIP-Relay1.A1_Switch_Terminal_A, D1.cathode
  N2: DIP-Relay1.A2_Switch_Terminal_A, Q2.E, D1.anode
  N3: U1.E, Part1.GND
  N4: U1.S, LCD1.V0
  N5: U1.A, Part1.5V
  N6: Q2.B, Part1.D3_PWM
  N7: Q2.C, LCD1.R/W, LCD1.LED-, Part2.GND, S1.leg1
  N8: Part1.A0, Part2.HORZ
  N9: Part1.A1, Part2.VERT
  N10: Part1.A3, S1.leg0
  N11: Part1.D8, LCD1.DB7
  N12: Part1.D0/RX, LCD1.RS
  N13: Part1.D1/TX, LCD1.E
  N14: Part1.D2, LCD1.DB4
  N15: Part1.D6_PWM, LCD1.DB5
  N16: Part1.D7, LCD1.DB6
  VDD: LCD1.VDD, LCD1.LED+, Part2.SEL, Part2.VCC
